# Fritzing sketch sound (saved by Fritzing 0.9.3b)

parts:
  X1 = USB Connectors [package=usb-mb-h]
  S1 = Toggle Switch [package=THT]
  S2 = Toggle Switch [package=THT]
  DFPlayer_Mini1 = DFPlayer MINI [package="DIP (Dual Inline) [THT]"]
  SP1 = SPEAKER [package=pcb_mount_speaker]
  Part1 = Arduino Uno (Rev3) - ICSP
  Part3 = Breakout Board for Electret Microphone
  Part4 = Breakout Board for Electret Microphone
  Part5 = Breakout Board for Electret Microphone
  R1 = Resistor [tolerance=±5% resistance=2.2k package=THT]
  LED3 = LEDs [package=led10mm]
  R5 = Resistor [tolerance=±5% resistance=1k package=THT]
  R6 = Resistor [tolerance=±5% resistance=1k package=THT]
  LED4 = LEDs [package=led10mm]
  LED5 = LEDs [package=led10mm]
  R7 = Resistor [tolerance=±5% resistance=2.2k package=THT]
  R8 = Resistor [tolerance=±5% resistance=2.2k package=THT]

nets:
  N1: X1.D+, S1.L1
  N2: X1.D-, S2.L2
  N3: X1.GND, DFPlayer_Mini1.GND#9
  N4: S1.COM, DFPlayer_Mini1.USB_+
  N5: S2.COM, DFPlayer_Mini1.USB_-
  VCC: DFPlayer_Mini1.VCC, Part1.5V, Part3.VCC, Part4.VCC, Part5.VCC
  N6: DFPlayer_Mini1.RX, R5.Pin_1
  N7: DFPlayer_Mini1.TX, R6.Pin_0
  N8: DFPlayer_Mini1.SPK1, SP1.+
  GND: DFPlayer_Mini1.GND#6, Part1.GND, Part3.GND, Part4.GND, Part5.GND
  N9: DFPlayer_Mini1.SPK2, SP1.-
  N10: Part1.A0, Part5.AUD
  N11: Part1.A1, Part3.AUD
  N12: Part1.A2, Part4.AUD
  N13: Part1.D9_PWM, R7.Pin_1
  N14: Part1.D0/RX, R6.Pin_1
  N15: Part1.D1/TX, R5.Pin_0
  N16: Part1.D3_PWM, R1.Pin_1
  N17: Part1.D6_PWM, R8.Pin_1
  N18: LED3.A, LED4.A, LED5.A

custom parts:
  DFPlayer MINI: MP3 module by DFRobot.com for playing Music from an SD-Card. Supports WAV and MP3 files.
